# Fritzing sketch Schematic_Wiring (saved by Fritzing 0.9.3b)
circuit board: 13.1462cm x 11.875cm
breadboards: 1

parts:
  ESP32 = TTGO T7-ESP32
  L_EYE_(wire1) = OLED 0.91" 128x32 I2C SSD1306 (GND/VCC)
  R_Eye_(wire) = OLED 0.91" 128x32 I2C SSD1306 (GND/VCC)
  MPU_(wire2) = Adafruit MPU6050
  Main_Batt = DC Power [voltage=12V]
  Motor_Driver = L298N DC motor driver
  M1 = DC Motor
  M2 = DC Motor
  S1 = Pushbutton [package=THT]

nets:
  GND: ESP32.GND, L_EYE_(wire1).GND, R_Eye_(wire).GND, MPU_(wire2).GND, Main_Batt.V-, Motor_Driver.GND
  N1: ESP32.26, Motor_Driver.IN2
  N2: ESP32.18, Motor_Driver.ENB
  N3: ESP32.33, MPU_(wire2).SCL
  N4: ESP32.23, Motor_Driver.ENA
  3V3: ESP32.3V3, MPU_(wire2).3.3V
  VCC: ESP32.5V, L_EYE_(wire1).VCC, R_Eye_(wire).VCC
  N5: ESP32.4, Motor_Driver.IN4
  N6: ESP32.21, L_EYE_(wire1).SCA, R_Eye_(wire).SCA
  N7: ESP32.32, MPU_(wire2).SDA
  N8: ESP32.22, L_EYE_(wire1).SCL, R_Eye_(wire).SCL
  N9: ESP32.25, Motor_Driver.IN1
  N10: ESP32.27, Motor_Driver.IN3
  N11: Motor_Driver.OUT1, M1.pin_2
  N12: Motor_Driver.OUT2, M1.pin_1
  N13: Motor_Driver.12V, Motor_Driver.5V-ENA-JMP-I, S1.leg0
  N14: Motor_Driver.OUT3, M2.pin_1
  N15: Motor_Driver.OUT4, M2.pin_2

notes:
  Probably SHOULD replace this with some kind of voltage regulator like the breadboard power supply shown in the video
  There MUST be a common ground between the ESP32 and L298N

custom parts:
  TTGO T7-ESP32: TTGO T7-ESP32 cpu module
  OLED 0.91" 128x32 I2C SSD1306 (GND/VCC): OLED 0.91" 128x32 I2C SSD1306 Pinout: GND/VCC/SCL/SDA
  Adafruit MPU6050: The MPU-6050 is a popular six axis accelerometer and gyroscope (gyro) that has all the info you need on how things are shakin' and spinnin' . With six axes of sensing and 16-bit measurements, you'll have everything you need to give your robot friend an inner ear. This combination of gyroscopes and accelerometers is commonly referred to as an Inertial Measurement Unit or IMU. Not so long ago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
  L298N DC motor driver: 2x DC motor driver with 78M05 positive voltage regulator (7..35 V) L298N: max 46 V, 2 A Set 5 V Enable jumper to enable 5 V regultor (needed for the L298N) and +5 V output at screw terminal or supply external +5 V at screw terminal Set ENA and/or ENB to +5 V to enable motor permanently or supply ENA and/or ENB with PWM signal IN1 and IN2 set rotation directory for motor A (OUT1/OUT2) IN2 and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
